# Fritzing sketch sketch1 (saved by Fritzing 0.9.2b)
breadboards: 1

parts:
  Parte1 = Arduino Uno (Rev3)
  U1 = LCD-16X2 [package=lcd-16x2_noholes]
  R1 = Rotary Potentiometer (Large) [maximum_resistance=100kΩ package=THT]
  S1 = Momentary Switch [package=ksa_sealed_tac_switch]
  S2 = Momentary Switch [package=ksa_sealed_tac_switch]
  R2 = Resistor [tolerance=±5% resistance=1k package="0603 [SMD]"]
  R3 = Resistor [tolerance=±0.05% resistance=1k package="0603 [SMD]"]
  LED1 = smd LED [color="Red (633nm)" package="0603 [SMD]"]
  LED2 = smd LED [color="Green (570nm)" package="0603 [SMD]"]
  R4 = Resistor [tolerance=±0.05% resistance=220 package="0603 [SMD]"]
  R5 = Resistor [tolerance=±0.05% resistance=220 package="0603 [SMD]"]

nets:
  N1: Parte1.D8, S1.4
  N2: Parte1.D9_PWM, R5.Pin_0
  N3: Parte1.D10_PWM/SS, R4.Pin_0
  N4: Parte1.D11_PWM/MOSI, U1.E
  N5: Parte1.D12/MISO, U1.RS
  N6: Parte1.D2, U1.DB7
  N7: Parte1.D3_PWM, U1.DB6
  N8: Parte1.D4, U1.DB5
  N9: Parte1.D5_PWM, U1.DB4
  N10: Parte1.D7, S2.4
  5V: Parte1.5V, U1.VDD, U1.A, R1.leg2, S1.1, S2.1
  GND: Parte1.GND, U1.VSS, U1.R_W, U1.K, R1.leg1, R2.Pin_0, R3.Pin_0, LED1.cathode
  N11: U1.VO, R1.wiper
  N12: S1.3, R3.Pin_1
  N13: S2.3, R2.Pin_1
  N14: LED1.anode, R4.Pin_1
  N15: LED2.cathode, R5.Pin_1
