# Fritzing sketch Esquema tarea1 (saved by Fritzing 0.8.7b)
breadboards: 1

parts:
  Parte1 = Arduino Uno (Rev3)
  LED1 = LED - 5mm [color="Red (633nm)" package="5 mm [THT]"]
  LED2 = LED - 5mm [color="Red (633nm)" package="5 mm [THT]"]
  R1 = Resistor [package="2010 [SMD]"]
  R2 = Resistor [tolerance=±5% resistance=220 package=THT]
  R3 = Rotary Potentiometer (Large) [maximum_resistance=100kΩ package=THT]
  S1 = Pushbutton [package="[THT]"]
  R4 = Resistor [tolerance=±20% resistance=10k package=THT]  # not connected

nets:
  N1: Parte1.A0, R3.wiper
  N2: Parte1.D12/MISO, R1.Pin_0
  N3: Parte1.D13/SCK, R2.Pin_0
  N4: Parte1.D2, S1.Pin_1, S1.Pin_2
  N5: Parte1.5V, R3.leg2, S1.Pin_3, S1.Pin_4
  N6: Parte1.GND, LED1.anode, LED2.anode, R3.leg1
  N7: LED1.cathode, R2.Pin_1
  N8: LED2.cathode, R1.Pin_1
