# Fritzing sketch Esquema_Tarea2 (saved by Fritzing 0.8.7b)
breadboards: 1

parts:
  Parte1 = Arduino Uno (Rev3)
  S1 = Pushbutton [package="[THT]"]
  R1 = Resistor [tolerance=±5% resistance=1k package=THT]
  LED1 = LED - 5mm [color="Red (633nm)" package="5 mm [THT]"]
  LED2 = LED - 5mm [color="Red (633nm)" package="5 mm [THT]"]
  LED3 = LED - 5mm [color="Green (570nm)" package="5 mm [THT]"]
  R2 = Resistor [tolerance=±5% resistance=220 package=THT]
  R3 = Resistor [tolerance=±5% resistance=220 package=THT]
  R4 = Resistor [tolerance=±5% resistance=220 package=THT]

nets:
  N1: Parte1.D8, R2.Pin_0
  N2: Parte1.D2, S1.Pin_1, S1.Pin_2, R1.Pin_0
  N3: Parte1.D6_PWM, R4.Pin_0
  N4: Parte1.D7, R3.Pin_0
  N5: Parte1.5V, S1.Pin_3, S1.Pin_4
  N6: Parte1.GND, R1.Pin_1, LED1.anode, LED2.anode, LED3.anode
  N7: LED1.cathode, R4.Pin_1
  N8: LED2.cathode, R2.Pin_1
  N9: LED3.cathode, R3.Pin_1
