# Fritzing sketch Esquema (saved by Fritzing 0.8.7b)
breadboards: 1

parts:
  Parte1 = Arduino Uno (Rev3)
  Parte2 = Arduino Uno (Rev3)
  R1 = Resistor [tolerance=±5% resistance=220 package=THT]
  R2 = Photocell (LDR) [package=THT]

nets:
  N1: Parte1.A0, R1.Pin_1, R2.pin_0
  N2: Parte1.A4/SDA, Parte2.A4/SDA
  N3: Parte1.A5/SCL, Parte2.A5/SCL
  N4: Parte1.5V, R1.Pin_0
  GND: Parte1.GND, Parte2.GND, R2.pin_1
