# Fritzing sketch Arduino uno (saved by Fritzing 0.9.2b)
breadboards: 1

parts:
  Parte1 = Arduino Uno (Rev3)
  U1 = LCD-16X2 [package=lcd-16x2_noholes]
  J1 = Basic Servo
  R1 = Rotary Potentiometer (Small) [maximum_resistance=100kΩ package=THT]
  R2 = Rotary Potentiometer (Small) [maximum_resistance=100kΩ package=THT]

nets:
  N1: Parte1.A0, R2.wiper
  N2: Parte1.D11_PWM/MOSI, U1.E
  N3: Parte1.D12/MISO, U1.RS
  N4: Parte1.D2, U1.DB7
  N5: Parte1.D3_PWM, U1.DB6
  N6: Parte1.D4, U1.DB5
  N7: Parte1.D5_PWM, U1.DB4
  N8: Parte1.D6_PWM, J1.pulse
  5V: Parte1.5V, U1.VDD, J1.vcc, R1.leg2, R2.leg2
  GND: Parte1.GND, U1.R_W, J1.gnd, R1.leg1, R2.leg1
  N9: U1.VO, R1.wiper
